# Fritzing sketch SENSOR_REVERSA_ESQUEMATICO (saved by Fritzing 0.9.3b)
breadboards: 1

parts:
  1 = LTE-302 [package=lte-302]
  SENSOR_DERECHA = hc-sr04
  Componente1 = Arduino Nano (Rev3.0)
  SENSOR_IZQUIERDA = hc-sr04
  SENSOR_ATRAS = hc-sr04
  2 = LTE-302 [package=lte-302]
  3 = LTE-302 [package=lte-302]
  R2 = Resistor [tolerance=±5% resistance=220 package="0603 [SMD]"]
  R3 = Resistor [tolerance=±5% resistance=220 package="0603 [SMD]"]
  R1 = Resistor [tolerance=±5% resistance=220 package="0603 [SMD]"]

nets:
  N1: 1.A, R1.Pin_0
  GND: 1.C, SENSOR_DERECHA.GND, Componente1.GND, SENSOR_IZQUIERDA.GND, SENSOR_ATRAS.GND, 2.C, 3.C
  N2: SENSOR_DERECHA.Trig, Componente1.D9
  N3: SENSOR_DERECHA.Echo, Componente1.D6
  N4: Componente1.D2, R1.Pin_1
  N5: Componente1.D3, R2.Pin_1
  N6: Componente1.D4, R3.Pin_1
  N7: Componente1.D7, SENSOR_IZQUIERDA.Echo
  N8: Componente1.D8, SENSOR_ATRAS.Echo
  N9: Componente1.D10, SENSOR_IZQUIERDA.Trig
  N10: Componente1.D11/MOSI, SENSOR_ATRAS.Trig
  N11: 2.A, R2.Pin_0
  N12: 3.A, R3.Pin_0
